// Logisim project 8080.circ as structural Verilog
module PC_8080 (
);

  wire Reset_out;
  wire [7:0] keyboard_1_data;
  wire [11:0] undriven;

  Button Reset (.out(Reset_out));
  System system_1 (.ResetIn(Reset_out));
  TTY #(.rows(25), .cols(80)) tty_1 (.data(undriven[6:0]), .clk(undriven[7]), .we(undriven[8]), .clr(undriven[9]));
  Keyboard keyboard_1 (
    .clk(undriven[7]), .re(undriven[10]), .clr(undriven[11]), .avail(keyboard_1_data[7]),
    .data(keyboard_1_data[6:0]));

  // Notes on the sheet:
  //   Key Input
endmodule

module System (
  input  ResetIn
);

  wire CLK, decoder_1_out0, decoder_1_out1, decoder_1_out2, decoder_1_out3, IRQ, n8080cpu_system_1_p8,
       n8080cpu_system_1_p9;
  wire [7:0] n8080cpu_system_1_p5;
  wire [9:0] counter_1_q;
  wire [15:0] n8080cpu_system_1_p7;

  Clock Clock (.out(CLK));
  Counter #(.width(10), .max('h3ff)) counter_1 (.Q(counter_1_q), .clk(CLK));  // open: load, D, count, carry, clr
  Pull_Resistor #(.pull(1)) pull_resistor_1 (.node(IRQ));
  LED led_1 (.in(counter_1_q[8]));
  // _8080CPU_SYSTEM 8080cpu_system_1: pin names not known; wires that end beside it: counter_1_q[8], CLK, ResetIn, IRQ, n8080cpu_system_1_p5, n8080cpu_system_1_p5, n8080cpu_system_1_p7, n8080cpu_system_1_p8, n8080cpu_system_1_p9
  // Probe on n8080cpu_system_1_p5
  // Probe on n8080cpu_system_1_p7
  Pull_Resistor #(.pull(1)) pull_resistor_2 (.node(n8080cpu_system_1_p9));
  Pull_Resistor #(.pull(1)) pull_resistor_3 (.node(n8080cpu_system_1_p5));
  Pull_Resistor pull_resistor_4 (.node(n8080cpu_system_1_p7));
  Pull_Resistor #(.pull(1)) pull_resistor_5 (.node(n8080cpu_system_1_p8));
  Decoder_part #(.select(2), .disabled(0), .enable("false")) decoder_1 (
    .out0(decoder_1_out0), .out1(decoder_1_out1), .out2(decoder_1_out2), .out3(decoder_1_out3),
    .sel(n8080cpu_system_1_p7[15:14]));
  ROM #(.addrWidth(14)) rom_1 (.addr(n8080cpu_system_1_p7[13:0]), .data(n8080cpu_system_1_p5), .sel(decoder_1_out0));
  RAM #(.addrWidth(14)) ram_1 (
    .addr(n8080cpu_system_1_p7[13:0]), .data(n8080cpu_system_1_p5), .sel(decoder_1_out1),
    .clk(n8080cpu_system_1_p9), .ld(n8080cpu_system_1_p8), .clr(1'b0));
  RAM #(.addrWidth(14)) ram_2 (
    .addr(n8080cpu_system_1_p7[13:0]), .data(n8080cpu_system_1_p5), .sel(decoder_1_out2),
    .clk(n8080cpu_system_1_p9), .ld(n8080cpu_system_1_p8), .clr(1'b0));
  RAM #(.addrWidth(14)) ram_3 (
    .addr(n8080cpu_system_1_p7[13:0]), .data(n8080cpu_system_1_p5), .sel(decoder_1_out3),
    .clk(n8080cpu_system_1_p9), .ld(n8080cpu_system_1_p8), .clr(1'b0));

  // Other names for the same wires on the sheet: Reset = ResetIn

  // Notes on the sheet:
  //   ROM0
  //   RAM0
  //   contents of rom_1 (hex, n*v repeats v):
  //   60 68 0 7b 0 7d 1f 0 5 bf e5 4 d7 fe 2 0 ee fe 7c 0 f 0 a5 8 e5 fb d6 9 fe e9 ff 48 65 6c 6c 6f 0 6e
  //   48 65 6c 6c 6f 43*0 76 1199*0 76 2553*0 f8 aa 8478*0 6e
  //   RAM1
  //   RAM2
endmodule

module _8080CPU_SYSTEM (
  input  [7:0] DataIn,
  input  IRQ,
  input  CLK,
  input  Reset,
  output [7:0] DataOut,
  output [15:0] AddressOut,
  output MEMR,
  output nWO,
  output INP,
  output OUT,
  output nRSTOUT
);

  wire and_1_out, and_2_out, CLK_t, d_ff_1_q, d_ff_1_qn, d_ff_2_q, d_ff_3_q, i8080_1_sync, not_1_out,
       not_2_out, not_3_out, not_4_out, not_6_out, not_8_out, not_9_out, P1, P2, PowerOnReset_q, xor_2_out;
  wire [3:0] counter_1_q;

  not not_1 (not_1_out, CLK);
  not not_2 (not_2_out, Reset);
  D_Flip_Flop d_ff_1 (.clk(not_1_out), .D(1'b0), .Q(d_ff_1_q), .Qn(d_ff_1_qn), .preset(not_3_out));  // open: en, reset
  not not_3 (not_3_out, and_1_out);
  D_Flip_Flop d_ff_2 (.clk(not_1_out), .D(d_ff_1_q), .Q(d_ff_2_q), .preset(not_4_out));  // open: Qn, en, reset
  not not_4 (not_4_out, and_1_out);
  and and_1 (and_1_out, not_2_out, PowerOnReset_q);
  D_Flip_Flop PowerOnReset (.clk(not_1_out), .D(1'b1), .Q(PowerOnReset_q));  // open: Qn, preset, en, reset
  not not_5 (CLK_t, not_1_out);
  D_Flip_Flop d_ff_3 (.clk(not_1_out), .D(d_ff_2_q), .Q(d_ff_3_q), .preset(not_6_out));  // open: Qn, en, reset
  not not_6 (not_6_out, and_1_out);
  i8080 i8080_1 (
    .DATA_BUS_in(DataIn), .DATA_BUS_out(DataOut), .ADDRESS_OUT(AddressOut), .P2(P2), .P1(P1),
    .nReset(nRSTOUT), .IRQ(IRQ), .SYNC(i8080_1_sync));  // open: HLTA
  not not_7 (nRSTOUT, d_ff_3_q);
  Counter #(.width(4), .max('hf)) counter_1 (
    .load(and_2_out), .D(4'b0011), .count(not_8_out), .Q(counter_1_q), .clk(CLK_t), .clr(not_9_out));  // open: carry
  not not_8 (not_8_out, and_2_out);
  not not_9 (not_9_out, and_1_out);
  and and_2 (and_2_out, counter_1_q[2], counter_1_q[3]);
  xor xor_1 (P2, counter_1_q[3], 1'b0);
  xor xor_2 (xor_2_out, counter_1_q[0], counter_1_q[1]);
  and and_3 (P1, xor_2_out, counter_1_q[2]);

  // Other names for the same wires on the sheet: nRST = nRSTOUT

  // Notes on the sheet:
  //   Reset: pull=up
  //   LogiSimのシミュレーションリセット対応
  //   DataBus
  //   AddressBus
endmodule

module i8080 (
  input  [7:0] DATA_BUS_in,
  input  [15:0] ADDRESS_OUT,
  input  IRQ,
  input  P2,
  input  P1,
  input  nReset,
  output [7:0] DATA_BUS_out,
  output SYNC,
  output HLTA
);

  wire address_latch_1_out_6, timing_and_control_1_aluctrl_2;
  wire [4:0] alu_1_toflag, flag_1_toalu, flag_1_todecoder;
  wire [7:0] acc_1_monitor, acc_1_thru, acc_1_toact, act_1_monitor, act_1_toalu, address_latch_1_lo_2,
       databus_buffer_1_monitor, flag_1_todatabus, instructin_register_1_monitor,
       instructin_register_1_opecodeout, INTERNAL_DATABUS, multiplexer_1_toregister_array_lo,
       n8bitgpreg_h_1_ctrlout, n8bitgpreg_h_1_monitor, n8bitgpreg_h_1_todbus, n8bitgpreg_h_1_toincdec,
       n8bitgpreg_h_2_ctrlout, n8bitgpreg_h_2_monitor, n8bitgpreg_h_2_todbus, n8bitgpreg_h_2_toincdec,
       n8bitgpreg_h_3_ctrlout, n8bitgpreg_h_3_monitor, n8bitgpreg_h_3_todbus, n8bitgpreg_h_3_toincdec,
       n8bitgpreg_h_4_ctrlout, n8bitgpreg_h_4_monitor, n8bitgpreg_h_4_todbus, n8bitgpreg_h_4_toincdec,
       n8bitgpreg_h_5_ctrlout, n8bitgpreg_h_5_monitor, n8bitgpreg_h_5_todbus, n8bitgpreg_h_5_toincdec,
       n8bitgpreg_h_6_ctrlout, n8bitgpreg_h_6_monitor, n8bitgpreg_h_6_todbus, n8bitgpreg_h_6_toincdec,
       n8bitgpreg_l_1_monitor, n8bitgpreg_l_1_todbus, n8bitgpreg_l_1_toincdec, n8bitgpreg_l_2_monitor,
       n8bitgpreg_l_2_todbus, n8bitgpreg_l_2_toincdec, n8bitgpreg_l_3_monitor, n8bitgpreg_l_3_todbus,
       n8bitgpreg_l_3_toincdec, n8bitgpreg_l_4_monitor, n8bitgpreg_l_4_todbus, n8bitgpreg_l_4_toincdec,
       n8bitgpreg_l_5_monitor, n8bitgpreg_l_5_todbus, n8bitgpreg_l_5_toincdec, n8bitgpreg_l_6_monitor,
       n8bitgpreg_l_6_todbus, n8bitgpreg_l_6_toincdec, register_selector_1_bc_ctrl,
       register_selector_1_de_ctrl, register_selector_1_hl_ctrl, register_selector_1_pc_ctrl,
       register_selector_1_sp_ctrl, register_selector_1_wz_ctrl, temp_reg_1_monitor, temp_reg_1_toalu,
       undriven, undriven_2;
  wire [9:0] alu_1_todaa, decimal_adjust_1_toalu, timing_and_control_1_state_out;
  wire [11:0] timing_and_control_1_accctrl;
  wire [15:0] address_latch_1_monitor, address_latch_1_monitor_2, address_latch_1_out;
  wire [23:0] timing_and_control_1_aluctrl;
  wire [31:0] decoder_1_ctrlout, timing_and_control_1_ctrl;

  // Probe on acc_1_monitor
  // Probe on act_1_monitor
  ACC acc_1 (
    .fromDATA_BUS(INTERNAL_DATABUS), .ctrl(timing_and_control_1_accctrl), .toACT(acc_1_toact),
    .THRU(acc_1_thru), .Monitor(acc_1_monitor), .toDATA_BUS(INTERNAL_DATABUS));
  // Probe on temp_reg_1_monitor
  ACT act_1 (
    .fromAcc(acc_1_toact), .toALU(act_1_toalu), .AccTHRU(acc_1_thru), .ctrl(timing_and_control_1_accctrl),
    .Monitor(act_1_monitor));
  // Probe on timing_and_control_1_accctrl
  STATE_IND state_ind_1 (.State_in(timing_and_control_1_state_out));  // open: out_2, out_3, out_4, out_5, out_6, out_7, out_8, out_9, out_10
  TEMP_REG temp_reg_1 (
    .fromDBUS(INTERNAL_DATABUS), .toALU(temp_reg_1_toalu), .ctrl(timing_and_control_1_accctrl),
    .monitor(temp_reg_1_monitor));
  TIMING_AND_CONTROL timing_and_control_1 (
    .AccCtrl(timing_and_control_1_accctrl), .P1(P1), .P2(P2), .ALUCtrl_2(timing_and_control_1_aluctrl_2),
    .nReset(nReset), .IRQ(IRQ), .ctrl(timing_and_control_1_ctrl), .ALUctrl(timing_and_control_1_aluctrl),
    .fromDECODER(decoder_1_ctrlout), .State_out(timing_and_control_1_state_out));
  // Probe on flag_1_todatabus
  FLAG flag_1 (
    .toALU(flag_1_toalu), .fromALU(alu_1_toflag), .ctrl(timing_and_control_1_aluctrl),
    .fromDATABUS(INTERNAL_DATABUS), .toDATABUS_2(INTERNAL_DATABUS), .toDECODER(flag_1_todecoder),
    .toDATABUS(flag_1_todatabus));
  ALU alu_1 (
    .S(timing_and_control_1_aluctrl), .B(temp_reg_1_toalu), .A(act_1_toalu), .ALU_OUT(INTERNAL_DATABUS),
    .toDAA(alu_1_todaa), .toFLAG(alu_1_toflag), .fromFLAG(flag_1_toalu), .fromDAA(decimal_adjust_1_toalu));
  DECIMAL_ADJUST decimal_adjust_1 (.fromALU(alu_1_todaa), .toALU(decimal_adjust_1_toalu));
  // Probe on databus_buffer_1_monitor
  // Probe on instructin_register_1_monitor
  // Probe on timing_and_control_1_aluctrl
  INSTRUCTIN_REGISTER instructin_register_1 (
    .OPECODEin(INTERNAL_DATABUS), .OPECODEout(instructin_register_1_opecodeout),
    .ctrl(timing_and_control_1_ctrl), .monitor(instructin_register_1_monitor));
  Decoder decoder_1 (
    .DataIn(instructin_register_1_opecodeout), .ctrlOut(decoder_1_ctrlout), .ctrl(timing_and_control_1_ctrl),
    .FlagIn(flag_1_todecoder));
  // Probe on timing_and_control_1_ctrl
  DATABUS_BUFFER databus_buffer_1 (
    .fromExDataBus(DATA_BUS_in), .toExDataBus(DATA_BUS_out), .toDataBus(INTERNAL_DATABUS),
    .fromDataBus(INTERNAL_DATABUS), .monitor(databus_buffer_1_monitor), .ctrl(timing_and_control_1_ctrl));
  REGISTER_SELECTOR register_selector_1 (
    .BC_Ctrl(register_selector_1_bc_ctrl), .DE_ctrl(register_selector_1_de_ctrl),
    .HL_ctrl(register_selector_1_hl_ctrl), .WZ_Ctrl(register_selector_1_wz_ctrl),
    .SP_ctrl(register_selector_1_sp_ctrl), .PC_ctrl(register_selector_1_pc_ctrl),
    .ctrl(timing_and_control_1_ctrl));
  _8BitGPReg_H u_8bitgpreg_h_1 (
    .Monitor(n8bitgpreg_h_1_monitor), .fromDBUS(undriven_2), .toINCDEC(n8bitgpreg_h_1_toincdec),
    .Control(register_selector_1_wz_ctrl), .ctrlOut(n8bitgpreg_h_1_ctrlout), .toDBUS(n8bitgpreg_h_1_todbus),
    .fromINCDEC(n8bitgpreg_h_2_todbus));  // open: out_en, latch_en
  // Probe on n8bitgpreg_h_1_monitor
  _8BitGPReg_H u_8bitgpreg_h_2 (
    .Monitor(n8bitgpreg_h_2_monitor), .fromDBUS(n8bitgpreg_h_1_toincdec), .toINCDEC(n8bitgpreg_h_2_toincdec),
    .Control(register_selector_1_bc_ctrl), .ctrlOut(n8bitgpreg_h_2_ctrlout), .toDBUS(n8bitgpreg_h_2_todbus),
    .fromINCDEC(n8bitgpreg_h_3_todbus));  // open: out_en, latch_en
  // Probe on n8bitgpreg_h_2_monitor
  _8BitGPReg_H u_8bitgpreg_h_3 (
    .Monitor(n8bitgpreg_h_3_monitor), .fromDBUS(n8bitgpreg_h_2_toincdec), .toINCDEC(n8bitgpreg_h_3_toincdec),
    .Control(register_selector_1_de_ctrl), .ctrlOut(n8bitgpreg_h_3_ctrlout), .toDBUS(n8bitgpreg_h_3_todbus),
    .fromINCDEC(n8bitgpreg_h_4_todbus));  // open: out_en, latch_en
  // Probe on n8bitgpreg_h_3_monitor
  _8BitGPReg_H u_8bitgpreg_h_4 (
    .Monitor(n8bitgpreg_h_4_monitor), .fromDBUS(n8bitgpreg_h_3_toincdec), .toINCDEC(n8bitgpreg_h_4_toincdec),
    .Control(register_selector_1_hl_ctrl), .ctrlOut(n8bitgpreg_h_4_ctrlout), .toDBUS(n8bitgpreg_h_4_todbus),
    .fromINCDEC(n8bitgpreg_h_5_todbus));  // open: out_en, latch_en
  // Probe on n8bitgpreg_h_4_monitor
  _8BitGPReg_H u_8bitgpreg_h_5 (
    .Monitor(n8bitgpreg_h_5_monitor), .fromDBUS(n8bitgpreg_h_4_toincdec), .toINCDEC(n8bitgpreg_h_5_toincdec),
    .Control(register_selector_1_sp_ctrl), .ctrlOut(n8bitgpreg_h_5_ctrlout), .toDBUS(n8bitgpreg_h_5_todbus),
    .fromINCDEC(n8bitgpreg_h_6_todbus));  // open: out_en, latch_en
  // Probe on n8bitgpreg_h_5_monitor
  _8BitGPReg_H u_8bitgpreg_h_6 (
    .Monitor(n8bitgpreg_h_6_monitor), .fromDBUS(n8bitgpreg_h_5_toincdec), .toINCDEC(n8bitgpreg_h_6_toincdec),
    .Control(register_selector_1_pc_ctrl), .ctrlOut(n8bitgpreg_h_6_ctrlout), .toDBUS(n8bitgpreg_h_6_todbus),
    .fromINCDEC(undriven));  // open: out_en, latch_en
  // Probe on n8bitgpreg_h_6_monitor
  // Probe on address_latch_1_monitor
  _8BitGPReg_L u_8bitgpreg_l_1 (
    .Monitor(n8bitgpreg_l_1_monitor), .fromDBUS(multiplexer_1_toregister_array_lo),
    .toINCDEC(n8bitgpreg_l_1_toincdec), .Control(n8bitgpreg_h_1_ctrlout), .toDBUS(n8bitgpreg_l_1_todbus),
    .fromINCDEC(n8bitgpreg_l_2_todbus));  // open: out_7, out_8
  // Probe on n8bitgpreg_l_1_monitor
  _8BitGPReg_L u_8bitgpreg_l_2 (
    .Monitor(n8bitgpreg_l_2_monitor), .fromDBUS(n8bitgpreg_l_1_toincdec), .toINCDEC(n8bitgpreg_l_2_toincdec),
    .Control(n8bitgpreg_h_2_ctrlout), .toDBUS(n8bitgpreg_l_2_todbus), .fromINCDEC(n8bitgpreg_l_3_todbus));  // open: out_7, out_8
  // Probe on n8bitgpreg_l_2_monitor
  _8BitGPReg_L u_8bitgpreg_l_3 (
    .Monitor(n8bitgpreg_l_3_monitor), .fromDBUS(n8bitgpreg_l_2_toincdec), .toINCDEC(n8bitgpreg_l_3_toincdec),
    .Control(n8bitgpreg_h_3_ctrlout), .toDBUS(n8bitgpreg_l_3_todbus), .fromINCDEC(n8bitgpreg_l_4_todbus));  // open: out_7, out_8
  // Probe on n8bitgpreg_l_3_monitor
  _8BitGPReg_L u_8bitgpreg_l_4 (
    .Monitor(n8bitgpreg_l_4_monitor), .fromDBUS(n8bitgpreg_l_3_toincdec), .toINCDEC(n8bitgpreg_l_4_toincdec),
    .Control(n8bitgpreg_h_4_ctrlout), .toDBUS(n8bitgpreg_l_4_todbus), .fromINCDEC(n8bitgpreg_l_5_todbus));  // open: out_7, out_8
  // Probe on n8bitgpreg_l_4_monitor
  _8BitGPReg_L u_8bitgpreg_l_5 (
    .Monitor(n8bitgpreg_l_5_monitor), .fromDBUS(n8bitgpreg_l_4_toincdec), .toINCDEC(n8bitgpreg_l_5_toincdec),
    .Control(n8bitgpreg_h_5_ctrlout), .toDBUS(n8bitgpreg_l_5_todbus), .fromINCDEC(n8bitgpreg_l_6_todbus));  // open: out_7, out_8
  // Probe on n8bitgpreg_l_5_monitor
  _8BitGPReg_L u_8bitgpreg_l_6 (
    .Monitor(n8bitgpreg_l_6_monitor), .fromDBUS(n8bitgpreg_l_5_toincdec), .toINCDEC(n8bitgpreg_l_6_toincdec),
    .Control(n8bitgpreg_h_6_ctrlout), .toDBUS(n8bitgpreg_l_6_todbus), .fromINCDEC(address_latch_1_lo_2));  // open: out_7, out_8
  // Probe on n8bitgpreg_l_6_monitor
  MULTIPLEXER multiplexer_1 (
    .fromDATABUS(INTERNAL_DATABUS), .toDATABUS(INTERNAL_DATABUS),
    .toREGISTER_ARRAY_hi(n8bitgpreg_h_1_todbus), .fromREGISTER_ARRAY_hi(undriven_2),
    .ctrl(timing_and_control_1_ctrl), .toREGISTER_ARRAY_lo(multiplexer_1_toregister_array_lo),
    .fromREGISTER_ARRAY_lo(n8bitgpreg_l_1_todbus));
  ADDRESS_LATCH address_latch_1 (
    .HI(undriven), .LO(n8bitgpreg_l_6_toincdec), .OUT(address_latch_1_out), .ctrl(timing_and_control_1_ctrl),
    .out_6(address_latch_1_out_6), .monitor_2(address_latch_1_monitor_2), .monitor(address_latch_1_monitor),
    .LO_2(address_latch_1_lo_2), .HI_2(n8bitgpreg_h_6_toincdec));
  // Probe on address_latch_1_monitor_2
  ADDRESS_BUFFER address_buffer_1 (
    .in_1(address_latch_1_out), .out_3(ADDRESS_OUT), .ctrl(timing_and_control_1_aluctrl_2));
  // Probe on INTERNAL_DATABUS

  // Notes on the sheet:
  //   ACCUMRATOR
  //   ACCUMRATOR
  //   LATCH
  //   Figure 2-2 8080 CPU Functional Block Diagram
  //   TEMP. REG.
  //   DECIMAL
  //   ADJUST
  //   DATA BUS
  //   BUFFER/LATCH
  //   INSTRUCTION
  //   REGISTER
  //   W
  //   B
  //   D
  //   H
  //   SPH
  //   PCH
  //   MULTIPLEXER
  //   Z
  //   C
  //   E
  //   L
  //   SPL
  //   PCL
  //   REGISTER
  //   ARRAY
endmodule

module CLK_GEN (
  input  CLK,
  input  Reset,
  output Q,
  output nRST
);

  wire and_1_out, d_ff_1_q, d_ff_1_qn, d_ff_2_q, d_ff_3_q, not_1_out, not_2_out, not_3_out, not_4_out,
       not_5_out, PowerOnReset_q;

  not not_1 (not_1_out, CLK);
  not not_2 (not_2_out, Reset);
  D_Flip_Flop d_ff_1 (.clk(not_1_out), .D(1'b0), .Q(d_ff_1_q), .Qn(d_ff_1_qn), .preset(not_3_out));  // open: en, reset
  not not_3 (not_3_out, and_1_out);
  D_Flip_Flop PowerOnReset (.clk(not_1_out), .D(1'b1), .Q(PowerOnReset_q));  // open: Qn, preset, en, reset
  D_Flip_Flop d_ff_2 (.clk(not_1_out), .D(d_ff_1_q), .Q(d_ff_2_q), .preset(not_4_out));  // open: Qn, en, reset
  not not_4 (not_4_out, and_1_out);
  not not_5 (not_5_out, and_1_out);
  and and_1 (and_1_out, not_2_out, PowerOnReset_q);
  not not_6 (Q, not_1_out);
  D_Flip_Flop d_ff_3 (.clk(not_1_out), .D(d_ff_2_q), .Q(d_ff_3_q), .preset(not_5_out));  // open: Qn, en, reset
  not not_7 (nRST, d_ff_3_q);

  // Notes on the sheet:
  //   LogiSimのシミュレーションリセット対応
endmodule

module Decoder (
  input  [7:0] DataIn,
  input  [4:0] FlagIn,
  input  [31:0] ctrl,
  output [31:0] ctrlOut
);

  wire ALUOPrI, ALUOPrM, ALUOPrr, and_9_out, and_10_out, and_20_out, and_24_out, and_30_out, and_33_out,
       and_37_out, block00, block01, block10, block11, CALL, CALLop, CMA, DAA, DAD, decoder_2_out0,
       decoder_2_out1, decoder_2_out2, decoder_2_out3, decoder_2_out4, decoder_2_out5, decoder_2_out6,
       decoder_2_out7, decoder_3_out0, decoder_3_out1, decoder_3_out2, decoder_3_out3, decoder_4_out0,
       decoder_4_out1, decoder_4_out2, decoder_4_out3, decoder_4_out4, decoder_4_out5, decoder_4_out6,
       decoder_4_out7, DoBranch, DST_M, HALT, IF, JUMPop, LXI, MOVI_r, MOVMr, MOVrM, MOVrr,
       multiplexer_1_out, NOP, not_1_out, not_2_out, not_3_out, not_4_out, not_5_out, OP1_r, OP1_x, PCHL,
       POP, priority_encoder_1_gs, PUSH, RET, RETop, rotate, RST, SPHL, SRC_M, XCHG, XTHL;
  wire [3:0] priority_encoder_1_out;

  and and_1 (CMA, DataIn[0], DataIn[1], DataIn[2], DataIn[3], ~DataIn[4], DataIn[5], ~DataIn[6], ~DataIn[7]);  // AND_Gate
  Decoder_part #(.select(2), .disabled(0), .enable("false")) decoder_1 (
    .out0(block00), .out1(block01), .out2(block10), .out3(block11), .sel(DataIn[7:6]));
  and and_2 (SRC_M, ~DataIn[0], DataIn[1], DataIn[2]);  // AND_Gate
  and and_3 (DST_M, ~DataIn[3], DataIn[4], DataIn[5]);  // AND_Gate
  and and_4 (CALLop, ~DataIn[1], DataIn[2], block11);  // AND_Gate
  and and_5 (JUMPop, DataIn[1], ~DataIn[2], block11);  // AND_Gate
  and and_6 (RETop, ~DataIn[1], ~DataIn[2], block11);  // AND_Gate
  and and_7 (RST, DataIn[0], DataIn[1], DataIn[2], DataIn[6], DataIn[7]);
  nor nor_1 (NOP, DataIn[0], DataIn[1], DataIn[2], DataIn[6], DataIn[7]);
  and and_8 (OP1_r, block00, DataIn[1], ~DataIn[2]);  // AND_Gate
  and and_9 (and_9_out, block01, SRC_M);
  and and_10 (and_10_out, block01, DST_M);
  and and_11 (HALT, DST_M, SRC_M, block01);
  and and_12 (ALUOPrr, block10, ~SRC_M);  // AND_Gate
  and and_13 (ALUOPrM, block10, SRC_M);
  and and_14 (ALUOPrI, SRC_M, block11);
  and and_15 (OP1_x, block00, ~DataIn[0], ~DataIn[1], DataIn[2]);  // AND_Gate
  and and_16 (rotate, block00, DataIn[0], DataIn[1], DataIn[2], ~DataIn[5]);  // AND_Gate
  and and_17 (IF, block11, DataIn[0], DataIn[1], ~DataIn[2], DataIn[4], DataIn[5]);  // AND_Gate
  nor nor_2 (MOVrr, ~block01, and_9_out, and_10_out, HALT);  // NOR_Gate
  and and_18 (MOVrM, and_9_out, ~HALT);  // AND_Gate
  and and_19 (MOVMr, and_10_out, ~HALT);  // AND_Gate
  and and_20 (and_20_out, block00, DataIn[0], ~DataIn[1], ~DataIn[2]);  // AND_Gate
  not not_1 (not_1_out, DataIn[3]);
  and and_21 (LXI, and_20_out, DataIn[3]);
  and and_22 (DAD, and_20_out, not_1_out);
  Multiplexer #(.select(2), .disabled(0), .enable("false")) multiplexer_1 (
    .in0(FlagIn[3]), .in1(FlagIn[0]), .in2(FlagIn[1]), .in3(FlagIn[4]), .out(multiplexer_1_out),
    .sel(DataIn[5:4]));
  xor xor_1 (DoBranch, multiplexer_1_out, ~DataIn[3]);  // XOR_Gate
  and and_23 (MOVI_r, block00, ~DataIn[0], DataIn[1], DataIn[2]);  // AND_Gate
  and and_24 (and_24_out, block11, DataIn[0], ~DataIn[1], DataIn[2]);  // AND_Gate
  not not_2 (not_2_out, DataIn[3]);
  and and_25 (XCHG, block11, DataIn[0], DataIn[1], ~DataIn[2], DataIn[3], ~DataIn[4], DataIn[5]);  // AND_Gate
  and and_26 (CALL, and_24_out, DataIn[3]);
  and and_27 (PUSH, and_24_out, not_2_out);
  and and_28 (rotate, block00, DataIn[0], DataIn[1], DataIn[2], ~DataIn[5]);  // AND_Gate
  and and_29 (DAD, block00, DataIn[0], ~DataIn[1], ~DataIn[2], DataIn[3]);  // AND_Gate
  and and_30 (and_30_out, block11, DataIn[0], ~DataIn[1], ~DataIn[2]);  // AND_Gate
  not not_3 (not_3_out, DataIn[3]);
  and and_31 (RET, and_30_out, DataIn[3], ~DataIn[5]);  // AND_Gate
  and and_32 (POP, and_30_out, not_3_out);
  and and_33 (and_33_out, block11, DataIn[0], ~DataIn[1], ~DataIn[2], DataIn[3], DataIn[5]);  // AND_Gate
  not not_4 (not_4_out, DataIn[4]);
  and and_34 (XTHL, block11, SRC_M, ~DataIn[3], ~DataIn[4], DataIn[5]);  // AND_Gate
  and and_35 (PCHL, not_4_out, and_33_out);
  and and_36 (SPHL, and_33_out, DataIn[4]);
  Decoder_part #(.select(3), .disabled(0), .enable("false")) decoder_2 (
    .out0(decoder_2_out0), .out1(decoder_2_out1), .out2(decoder_2_out2), .out3(decoder_2_out3),
    .out4(decoder_2_out4), .out5(decoder_2_out5), .out6(decoder_2_out6), .out7(decoder_2_out7),
    .sel(DataIn[5:3]));
  Decoder_part #(.select(2), .disabled(0), .enable("false")) decoder_3 (
    .out0(decoder_3_out0), .out1(decoder_3_out1), .out2(decoder_3_out2), .out3(decoder_3_out3),
    .sel(DataIn[5:4]));
  Priority_Encoder #(.select(4)) priority_encoder_1 (
    .out(priority_encoder_1_out), .gs(priority_encoder_1_gs));  // open: in0, in1, in2, in3, in4, in5, in6, in7, in8, in9, in10, in11, in12, in13, in14, in15, en_out, en_in
  Decoder_part #(.select(3), .disabled(0), .enable("false")) decoder_4 (
    .out0(decoder_4_out0), .out1(decoder_4_out1), .out2(decoder_4_out2), .out3(decoder_4_out3),
    .out4(decoder_4_out4), .out5(decoder_4_out5), .out6(decoder_4_out6), .out7(decoder_4_out7),
    .sel(DataIn[2:0]));
  and and_37 (and_37_out, block00, DataIn[0], DataIn[1], DataIn[2], ~DataIn[4], DataIn[5]);  // AND_Gate
  not not_5 (not_5_out, DataIn[3]);
  and and_38 (FlagIn[0], block00, DataIn[0], DataIn[1], DataIn[2], DataIn[4], DataIn[5]);
  and and_39 (DAA, and_37_out, not_5_out);
  and and_40 (CMA, and_37_out, DataIn[3]);

  // Other names for the same wires on the sheet: ALU_OP[2:0] = DataIn[5:3]; Bits_Mid[2:0] = DataIn[5:3];
  //   DataIn_t[7:0] = DataIn; DST_r[2:0] = DataIn[5:3]; RegX[1:0] = DataIn[5:4]; rotate_thruCY = DataIn[4];
  //   Bits_Lo[2:0] = DataIn[2:0]; OP1_ｒ_DEC = DataIn[0]; SRC_r[2:0] = DataIn[2:0]; CM_ST = DataIn[3];
  //   EI_DI = DataIn[3]; OP1_x_DEC = DataIn[3]; rotateR = DataIn[3]; CY = FlagIn[0]; PF = FlagIn[1]; AC = FlagIn[2];
  //   ZF = FlagIn[3]; SF = FlagIn[4]

  // Notes on the sheet:
  //   _DECフラグは1の時DEC
  //   B
  //   C
  //   D
  //   E
  //   H
  //   L
  //   M
  //   A
  //   BC
  //   DE
  //   HL
  //   SP
  //   B
  //   C
  //   D
  //   E
  //   H
  //   L
  //   M
  //   A
endmodule

module ALU (
  input  [23:0] S,
  input  [7:0] B,
  input  [7:0] A,
  input  [4:0] fromFLAG,
  input  [9:0] fromDAA,
  output [4:0] toFLAG,
  output [7:0] ALU_OUT,
  output [9:0] toDAA
);

  wire alu8a_1_cy, multiplexer_2_out;
  wire [7:0] alu8a_1_y, alu8l_1_y, multiplexer_1_out, multiplexer_4_out;
  wire [7:7] undriven;

  Multiplexer #(.width(8), .disabled(0), .enable("false")) multiplexer_1 (
    .in0(A), .in1(8'h38), .out(multiplexer_1_out), .sel(S[9]));
  ALU8L alu8l_1 (.A(multiplexer_1_out), .B(B), .S(S[7:4]), .Y(alu8l_1_y));
  ALU8A alu8a_1 (.B(alu8l_1_y), .A(multiplexer_1_out), .Cin(S[10]), .CY(alu8a_1_cy), .Y(alu8a_1_y));  // open: AC
  Multiplexer #(.disabled(0), .enable("false")) multiplexer_2 (
    .in0(multiplexer_1_out[0]), .in1(multiplexer_1_out[7]), .out(multiplexer_2_out), .sel(S[17]));
  Multiplexer #(.select(2), .disabled(0), .enable("false")) multiplexer_3 (
    .in0(alu8a_1_cy), .in1(multiplexer_2_out), .in3(fromDAA[1]), .out(toFLAG[0]), .sel(S[1:0]));  // open: in2
  Multiplexer #(.select(2), .width(8), .disabled(0), .enable("false")) multiplexer_4 (
    .in0(alu8a_1_y), .in1(alu8l_1_y), .in2({undriven[7], multiplexer_1_out[7:1]}),
    .in3({multiplexer_1_out[6:0], S[10]}), .out(multiplexer_4_out), .sel(S[3:2]));
  EvenPrity evenprity_1 (.A(ALU_OUT), .Y(toFLAG[1]));
  ZeroFlag zeroflag_1 (.A(ALU_OUT), .Y(toFLAG[3]));
  Multiplexer #(.width(8), .disabled(0), .enable("false")) multiplexer_5 (
    .in0(multiplexer_4_out), .in1(fromDAA[9:2]), .out(ALU_OUT), .sel(S[8]));

  assign toDAA = {A, fromFLAG[0], fromFLAG[2]};
  assign {toFLAG[4], toFLAG[2]} = {ALU_OUT[7], fromDAA[0]};
endmodule

module ZeroFlag (
  input  [7:0] A,
  output Y
);

  nor nor_1 (Y, A[0], A[1], A[2], A[3], A[4], A[5], A[6], A[7]);
endmodule

// EP
module EvenPrity (
  input  [7:0] A,
  output Y
);

  NotExactlyOne xnor_1 (
    .out(Y), .in0(A[0]), .in1(A[1]), .in2(A[2]), .in3(A[3]), .in4(A[4]), .in5(A[5]), .in6(A[6]), .in7(A[7]));
endmodule

module ALU8L (
  input  [7:0] A,
  input  [7:0] B,
  input  [3:0] S,
  output [7:0] Y
);

  Multiplexer #(.select(2), .disabled(0), .enable("false")) multiplexer_1 (
    .in0(S[0]), .in1(S[1]), .in2(S[2]), .in3(S[3]), .out(Y[4]), .sel({B[4], A[4]}));
  Multiplexer #(.select(2), .disabled(0), .enable("false")) multiplexer_2 (
    .in0(S[0]), .in1(S[1]), .in2(S[2]), .in3(S[3]), .out(Y[5]), .sel({B[5], A[5]}));
  Multiplexer #(.select(2), .disabled(0), .enable("false")) multiplexer_3 (
    .in0(S[0]), .in1(S[1]), .in2(S[2]), .in3(S[3]), .out(Y[6]), .sel({B[6], A[6]}));
  Multiplexer #(.select(2), .disabled(0), .enable("false")) multiplexer_4 (
    .in0(S[0]), .in1(S[1]), .in2(S[2]), .in3(S[3]), .out(Y[7]), .sel({B[7], A[7]}));
  Multiplexer #(.select(2), .disabled(0), .enable("false")) multiplexer_5 (
    .in0(S[0]), .in1(S[1]), .in2(S[2]), .in3(S[3]), .out(Y[0]), .sel({B[0], A[0]}));
  Multiplexer #(.select(2), .disabled(0), .enable("false")) multiplexer_6 (
    .in0(S[0]), .in1(S[1]), .in2(S[2]), .in3(S[3]), .out(Y[1]), .sel({B[1], A[1]}));
  Multiplexer #(.select(2), .disabled(0), .enable("false")) multiplexer_7 (
    .in0(S[0]), .in1(S[1]), .in2(S[2]), .in3(S[3]), .out(Y[2]), .sel({B[2], A[2]}));
  Multiplexer #(.select(2), .disabled(0), .enable("false")) multiplexer_8 (
    .in0(S[0]), .in1(S[1]), .in2(S[2]), .in3(S[3]), .out(Y[3]), .sel({B[3], A[3]}));
endmodule

module ALU4A (
  input  [3:0] B,
  input  [3:0] A,
  input  CIn,
  output COut,
  output [3:0] Y
);

  wire and_1_out, and_2_out, and_3_out, and_4_out, and_5_out, and_6_out, and_7_out, and_8_out, and_9_out,
       and_10_out, and_11_out, and_12_out, and_13_out, and_14_out, or_2_out, or_3_out, or_4_out, xor_1_out,
       xor_2_out, xor_3_out, xor_4_out;

  xor xor_1 (xor_1_out, B[3], A[3]);
  and and_1 (and_1_out, B[3], A[3]);
  xor xor_2 (xor_2_out, B[2], A[2]);
  and and_2 (and_2_out, B[2], A[2]);
  xor xor_3 (xor_3_out, B[1], A[1]);
  and and_3 (and_3_out, B[1], A[1]);
  xor xor_4 (xor_4_out, B[0], A[0]);
  and and_4 (and_4_out, B[0], A[0]);
  and and_5 (and_5_out, xor_1_out, and_2_out);
  and and_6 (and_6_out, xor_1_out, xor_2_out, and_3_out);
  and and_7 (and_7_out, xor_1_out, xor_2_out, xor_3_out, and_4_out);
  and and_8 (and_8_out, xor_1_out, xor_2_out, xor_3_out, xor_4_out, CIn);
  and and_9 (and_9_out, xor_2_out, and_3_out);
  and and_10 (and_10_out, xor_2_out, xor_3_out, and_4_out);
  and and_11 (and_11_out, xor_2_out, xor_3_out, xor_4_out, CIn);
  and and_12 (and_12_out, xor_3_out, and_4_out);
  and and_13 (and_13_out, xor_3_out, xor_4_out, CIn);
  and and_14 (and_14_out, xor_4_out, CIn);
  or or_1 (COut, and_1_out, and_5_out, and_6_out, and_7_out, and_8_out);
  or or_2 (or_2_out, and_2_out, and_9_out, and_10_out, and_11_out);
  or or_3 (or_3_out, and_3_out, and_12_out, and_13_out);
  or or_4 (or_4_out, and_4_out, and_14_out);
  xor xor_5 (Y[3], xor_1_out, or_2_out);
  xor xor_6 (Y[2], xor_2_out, or_3_out);
  xor xor_7 (Y[1], xor_3_out, or_4_out);
  xor xor_8 (Y[0], xor_4_out, CIn);
endmodule

module ALU8A (
  input  [7:0] B,
  input  [7:0] A,
  input  Cin,
  output CY,
  output [7:0] Y,
  output AC
);

  ALU4A alu4a_1 (.B(B[7:4]), .A(A[7:4]), .CIn(AC), .COut(CY), .Y(Y[7:4]));
  ALU4A alu4a_2 (.B(B[3:0]), .A(A[3:0]), .CIn(Cin), .COut(AC), .Y(Y[3:0]));
endmodule

module CarrySelector (
  input  CY,
  input  A7,
  input  OP0,
  input  OP1,
  output CC
);

  Multiplexer #(.select(2), .enable("false")) multiplexer_1 (
    .in0(CY), .in1(A7), .in2(1'b1), .in3(1'b0), .out(CC), .sel({OP1, OP0}));
endmodule

module ALU_OP (
  input  D,
  input  C,
  input  B,
  input  A,
  output op3,
  output op2,
  output op1,
  output op0
);

  wire and_1_out, and_2_out, and_3_out, and_4_out, and_5_out, and_6_out, and_7_out, and_8_out, and_9_out,
       and_10_out, not_1_out, not_2_out, not_3_out, not_4_out;

  not not_1 (not_1_out, D);
  not not_2 (not_2_out, C);
  not not_3 (not_3_out, B);
  not not_4 (not_4_out, A);
  and and_1 (and_1_out, not_1_out, not_2_out, not_3_out);
  and and_2 (and_2_out, C, not_4_out);
  and and_3 (and_3_out, D, A);
  and and_4 (and_4_out, not_3_out, A);
  and and_5 (and_5_out, C, B, not_4_out);
  and and_6 (and_6_out, C, A);
  and and_7 (and_7_out, D, A);
  and and_8 (and_8_out, not_2_out, B);
  and and_9 (and_9_out, B, A);
  and and_10 (and_10_out, D, A);
  or or_1 (op3, and_1_out, and_2_out, and_3_out);
  or or_2 (op2, and_1_out, and_4_out, and_5_out);
  or or_3 (op1, B, and_6_out, and_7_out);
  or or_4 (op0, and_8_out, and_9_out, and_10_out);
endmodule

module ADD_6 (
  input  a3,
  input  a2,
  input  a1,
  input  a0,
  input  ADD,
  output cy,
  output y3,
  output y2,
  output y1,
  output y0
);

  wire and_1_out, and_2_out, and_3_out, and_5_out, and_6_out, and_7_out, and_8_out, and_9_out, and_10_out,
       not_1_out, not_2_out, not_3_out, not_4_out, not_5_out, or_1_out, or_2_out;

  or or_1 (or_1_out, a2, a3);
  not not_1 (not_1_out, a3);
  not not_2 (not_2_out, a3);
  not not_3 (not_3_out, a1);
  not not_4 (not_4_out, a1);
  and and_1 (and_1_out, not_1_out, a1);
  and and_2 (and_2_out, not_2_out, not_3_out);
  and and_3 (and_3_out, a2, a1);
  or or_2 (or_2_out, and_2_out, and_3_out);
  not not_5 (not_5_out, ADD);
  and and_4 (cy, or_1_out, ADD);
  and and_5 (and_5_out, ADD, and_1_out);
  and and_6 (and_6_out, not_5_out, a3);
  and and_7 (and_7_out, ADD, or_2_out);
  and and_8 (and_8_out, not_5_out, a2);
  and and_9 (and_9_out, ADD, not_4_out);
  and and_10 (and_10_out, not_5_out, a1);
  or or_3 (y3, and_5_out, and_6_out);
  or or_4 (y2, and_7_out, and_8_out);
  or or_5 (y1, and_9_out, and_10_out);

  assign y0 = a0;
endmodule

// INC
module _4bit_addc_0 (
  input  cin,
  input  a3,
  input  a2,
  input  a1,
  input  a0,
  output y3,
  output y2,
  output y1,
  output y0
);

  wire and_1_out, and_2_out, and_3_out, and_4_out, and_5_out, and_6_out, and_7_out, and_8_out, and_9_out,
       and_10_out, and_11_out, and_12_out, and_13_out, and_14_out, not_1_out, not_2_out, not_3_out,
       not_4_out, not_5_out;

  not not_1 (not_1_out, cin);
  not not_2 (not_2_out, a3);
  not not_3 (not_3_out, a2);
  not not_4 (not_4_out, a1);
  not not_5 (not_5_out, a0);
  and and_1 (and_1_out, not_1_out, a3);
  and and_2 (and_2_out, a3, not_3_out);
  and and_3 (and_3_out, a3, not_4_out);
  and and_4 (and_4_out, a3, not_5_out);
  and and_5 (and_5_out, cin, not_2_out, a2, a1, a0);
  and and_6 (and_6_out, not_1_out, a2);
  and and_7 (and_7_out, a2, not_4_out);
  and and_8 (and_8_out, a2, not_5_out);
  and and_9 (and_9_out, cin, not_3_out, a1, a0);
  and and_10 (and_10_out, not_1_out, a1);
  and and_11 (and_11_out, a1, not_5_out);
  and and_12 (and_12_out, cin, not_4_out, a0);
  and and_13 (and_13_out, not_1_out, a0);
  and and_14 (and_14_out, cin, not_5_out);
  or or_1 (y3, and_1_out, and_2_out, and_3_out, and_4_out, and_5_out);
  or or_2 (y2, and_6_out, and_7_out, and_8_out, and_9_out);
  or or_3 (y1, and_10_out, and_11_out, and_12_out);
  or or_4 (y0, and_13_out, and_14_out);
endmodule

module DAA (
  input  [7:0] A,
  input  AC,
  input  Cin,
  output AC_2,
  output [7:0] Y,
  output Cout
);

  wire and_2_out, GT9_hi, GT9_lo, n4bit_addc_0_1_y0, n4bit_addc_0_1_y1, n4bit_addc_0_1_y2, n4bit_addc_0_1_y3,
       or_1_out, or_2_out, or_3_out;

  // Probe on A
  or or_1 (or_1_out, A[1], A[2]);
  and and_1 (GT9_lo, or_1_out, A[3]);
  or or_2 (or_2_out, GT9_lo, AC);
  ADD_6 add_6_1 (
    .a3(A[3]), .cy(AC_2), .a2(A[2]), .y3(Y[3]), .a1(A[1]), .y2(Y[2]), .y1(Y[1]), .a0(A[0]), .y0(Y[0]),
    .ADD(or_2_out));
  _4bit_addc_0 u_4bit_addc_0_1 (
    .cin(AC_2), .a3(A[7]), .a2(A[6]), .y3(n4bit_addc_0_1_y3), .a1(A[5]), .a0(A[4]), .y2(n4bit_addc_0_1_y2),
    .y1(n4bit_addc_0_1_y1), .y0(n4bit_addc_0_1_y0));
  and and_2 (and_2_out, AC_2, A[4]);
  or or_3 (or_3_out, and_2_out, A[5], A[6]);
  // Probe on Y
  ADD_6 add_6_2 (
    .a3(n4bit_addc_0_1_y3), .a2(n4bit_addc_0_1_y2), .y3(Y[7]), .a1(n4bit_addc_0_1_y1), .y2(Y[6]), .y1(Y[5]),
    .a0(n4bit_addc_0_1_y0), .y0(Y[4]), .ADD(Cout));  // open: cy
  and and_3 (GT9_hi, or_3_out, A[7]);
  or or_4 (Cout, Cin, GT9_hi);

  // Notes on the sheet:
  //   i8080Aは、このときのフラグがACに書き戻されるのだと思う 
endmodule

module TEMP_REG (
  input  [7:0] fromDBUS,
  input  [11:0] ctrl,
  output [7:0] monitor,
  output [7:0] toALU
);

  wire [7:0] multiplexer_1_out;

  Register register_1 (.D(fromDBUS), .en(ctrl[9]), .Q(monitor), .clk(ctrl[10]));  // open: clr
  assign toALU = ctrl[8] ? multiplexer_1_out : 8'bz;  // Controlled_Buffer controlled_buffer_1
  Multiplexer #(.width(8), .disabled(0), .enable("false")) multiplexer_1 (
    .in0(monitor), .in1(fromDBUS), .out(multiplexer_1_out), .sel(ctrl[11]));
endmodule

module ACC (
  input  [7:0] fromDATA_BUS,
  input  [11:0] ctrl,
  output [7:0] Monitor,
  output [7:0] toACT,
  output [7:0] toDATA_BUS,
  output [7:0] THRU
);

  Register register_1 (.D(fromDATA_BUS), .en(ctrl[1]), .Q(Monitor), .clk(ctrl[0]));  // open: clr
  Multiplexer #(.width(8), .disabled(0), .enable("false")) multiplexer_1 (
    .in0(Monitor), .in1(fromDATA_BUS), .out(toACT), .sel(ctrl[2]));
  assign toDATA_BUS = ctrl[3] ? toACT : 8'bz;  // Controlled_Buffer controlled_buffer_1

  assign THRU = fromDATA_BUS;
endmodule

module ACT (
  input  [7:0] fromAcc,
  input  [7:0] AccTHRU,
  input  [11:0] ctrl,
  output [7:0] Monitor,
  output [7:0] toALU
);

  wire undriven, undriven_2, undriven_3;
  wire [7:0] multiplexer_1_out;

  Multiplexer #(.width(8), .disabled(0), .enable("false")) multiplexer_1 (
    .in0(fromAcc), .in1(AccTHRU), .out(multiplexer_1_out));  // open: sel
  Register register_1 (.D(multiplexer_1_out), .en(undriven_2), .Q(Monitor), .clk(undriven));  // open: clr
  Multiplexer #(.width(8), .disabled(0), .enable("false")) multiplexer_2 (
    .in0(Monitor), .in1(multiplexer_1_out), .out(toALU), .sel(undriven_3));
endmodule

module TMP (
  input  [7:0] fromAcc,
  input  Latch,
  input  clk,
  input  OutEn_Thru,
  output [7:0] toALU
);

  wire [7:0] register_1_q;

  Register register_1 (.D(fromAcc), .en(Latch), .Q(register_1_q), .clk(clk));  // open: clr
  Multiplexer #(.width(8), .disabled(0), .enable("false")) multiplexer_1 (
    .in0(register_1_q), .in1(fromAcc), .out(toALU), .sel(OutEn_Thru));
endmodule

module Carry (
  input  CarryIn,
  input  [1:0] CarryOutCtrl,
  input  [1:0] CarryInCtrl,
  input  CarrySrcSel,
  input  fromALU,
  output CarryOut,
  output toALU
);

  wire multiplexer_2_out, not_1_out, not_2_out;

  not not_1 (not_1_out, multiplexer_2_out);
  Multiplexer #(.select(2), .disabled(0), .enable("false")) multiplexer_1 (
    .in0(multiplexer_2_out), .in1(not_1_out), .in2(1'b1), .in3(1'b0), .out(CarryOut), .sel(CarryOutCtrl));
  Multiplexer #(.disabled(0), .enable("false")) multiplexer_2 (
    .in0(toALU), .in1(fromALU), .out(multiplexer_2_out), .sel(CarrySrcSel));
  Multiplexer #(.select(2), .disabled(0), .enable("false")) multiplexer_3 (
    .in0(CarryIn), .in1(not_2_out), .in2(1'b1), .in3(1'b0), .out(toALU), .sel(CarryInCtrl));
  not not_2 (not_2_out, CarryIn);
endmodule

module Flag_Flip_Flop (
  input  [1:0] CarryOutCtrl,
  input  [1:0] CarryInCtrl,
  input  CarrySrcSel,
  input  fromALU,
  output toALU
);

  wire CY_q, multiplexer_1_out, multiplexer_2_out, not_1_out, not_2_out, undriven;

  not not_1 (not_1_out, multiplexer_2_out);
  Multiplexer #(.select(2), .disabled(0), .enable("false")) multiplexer_1 (
    .in0(multiplexer_2_out), .in1(not_1_out), .in2(1'b1), .in3(1'b0), .out(multiplexer_1_out),
    .sel(CarryOutCtrl));
  Register #(.width(4)) Flags ();  // open: D, en, Q, clk, clr
  Multiplexer #(.disabled(0), .enable("false")) multiplexer_2 (
    .in0(toALU), .in1(fromALU), .out(multiplexer_2_out), .sel(CarrySrcSel));
  Register #(.width(1)) CY (.D(undriven), .Q(CY_q));  // open: en, clk, clr
  Multiplexer #(.select(2), .disabled(0), .enable("false")) multiplexer_3 (
    .in0(undriven), .in1(not_2_out), .in2(1'b1), .in3(1'b0), .out(toALU), .sel(CarryInCtrl));
  not not_2 (not_2_out, undriven);
endmodule

module _2layerClock (
  input  A3,
  input  A2,
  input  A1,
  input  A0,
  output P2,
  output P1
);

  wire and_1_out, and_2_out, and_3_out, and_4_out, not_1_out, not_2_out, not_3_out, not_4_out;

  not not_1 (not_1_out, A3);
  not not_2 (not_2_out, A2);
  not not_3 (not_3_out, A1);
  not not_4 (not_4_out, A0);
  and and_1 (and_1_out, not_1_out, A1, A0);
  and and_2 (and_2_out, not_1_out, A2);
  and and_3 (and_3_out, not_1_out, not_2_out, not_3_out, A0);
  and and_4 (and_4_out, not_1_out, not_2_out, A1, not_4_out);
  or or_1 (P2, and_1_out, and_2_out);
  or or_2 (P1, and_3_out, and_4_out);
endmodule

module _8BitGPReg_H (
  input  [7:0] fromINCDEC,
  input  [7:0] fromDBUS,
  input  [7:0] Control,
  output [7:0] Monitor,
  output [7:0] toDBUS,
  output [7:0] toINCDEC,
  output out_en,
  output latch_en,
  output [7:0] ctrlOut
);

  Register register_1 (.D(fromDBUS), .en(Control[6]), .Q(Monitor), .clk(Control[0]));  // open: clr
  assign fromDBUS = Control[4] ? Monitor : 8'bz;  // Controlled_Buffer controlled_buffer_1
  assign fromDBUS = Control[4] ? Monitor : 8'bz;  // Controlled_Buffer controlled_buffer_2

  assign ctrlOut = Control;
  assign fromINCDEC = fromDBUS;
  assign latch_en = Control[6];
  assign out_en = Control[4];
  assign toDBUS = fromDBUS;
  assign toINCDEC = fromDBUS;
endmodule

module _8BitGPReg_L (
  input  [7:0] fromINCDEC,
  input  [7:0] fromDBUS,
  input  [7:0] Control,
  output [7:0] Monitor,
  output [7:0] toDBUS,
  output [7:0] toINCDEC,
  output out_7,
  output out_8
);

  Register register_1 (.D(fromINCDEC), .en(Control[5]), .Q(Monitor), .clk(Control[7]));  // open: clr
  assign fromDBUS = Control[3] ? Monitor : 8'bz;  // Controlled_Buffer controlled_buffer_1

  assign out_7 = Control[3];
  assign out_8 = Control[5];
  assign toDBUS = fromINCDEC;
  assign toINCDEC = fromDBUS;
endmodule

module TIMING_AND_CONTROL (
  input  [31:0] fromDECODER,
  input  nReset,
  input  P1,
  input  P2,
  input  IRQ,
  output [23:0] ALUctrl,
  output [11:0] AccCtrl,
  output ALUCtrl_2,
  output [31:0] ctrl,
  output [9:0] State_out
);

  wire internalRESET_q, not_1_out, skipM1T5;
  wire [1:0] statedecoder_1_t;
  wire [2:0] register_2_q, statedecoder_1_m, undriven;
  wire [4:0] getnextstate_1_next, register_1_q;
  wire [31:2] undriven_2;

  not not_1 (not_1_out, nReset);
  D_Flip_Flop internalRESET (.clk(P1), .D(not_1_out), .Q(internalRESET_q));  // open: Qn, preset, en, reset
  D_Flip_Flop INTE ();  // open: clk, D, Q, Qn, preset, en, reset
  D_Flip_Flop INT ();  // open: clk, D, Q, Qn, preset, en, reset
  D_Flip_Flop HOLD ();  // open: clk, D, Q, Qn, preset, en, reset
  Register #(.width(5)) register_1 (.D(getnextstate_1_next), .Q(register_1_q), .clk(P2));  // open: en, clr
  Register #(.width(3)) register_2 (.D(undriven), .Q(register_2_q), .clk(P2));  // open: en, clr
  GetNextState getnextstate_1 (
    .state(register_1_q), .\type (register_2_q), .next(getnextstate_1_next), .SkipN1T5(skipM1T5));
  // Probe on statedecoder_1_m
  StateDecoder statedecoder_1 (.A(getnextstate_1_next), .M(statedecoder_1_m), .T(statedecoder_1_t));
  // Probe on statedecoder_1_t
  Decoder_part #(.select(3), .disabled(0), .enable("false")) decoder_1 (
    .out0(State_out[0]), .out1(State_out[1]), .out2(State_out[2]), .out3(State_out[3]), .out4(State_out[4]),
    .sel(statedecoder_1_m));  // open: out5, out6, out7
  Decoder_part #(.select(2), .disabled(0), .enable("false")) decoder_2 (
    .out0(State_out[5]), .out1(State_out[6]), .out2(State_out[7]), .out3(State_out[8]), .sel(statedecoder_1_t));
  Register #(.width(32)) register_3 (.D({undriven_2, P2, P1}), .Q(ctrl));  // open: en, clk, clr

  assign ALUctrl[1:0] = {P2, P1};
  assign ALUCtrl_2 = 1'b0;

  // Notes on the sheet:
  //   nReset: pull=up
endmodule

// INC/DEC ADDRESS LATCH
module ADDRESS_LATCH (
  input  [7:0] LO,
  input  [7:0] HI,
  input  [31:0] ctrl,
  output [15:0] monitor,
  output [15:0] OUT,
  output out_6,
  output [7:0] LO_2,
  output [7:0] HI_2,
  output [15:0] monitor_2
);

  wire undriven;
  wire [15:0] dec16_1_out_2, inc16_1_out_2;

  Register #(.width(16)) register_1 (.D({HI, LO}), .en(ctrl[28]), .Q(OUT), .clk(undriven));  // open: clr
  INC16 inc16_1 (.in_1(OUT), .out_2(inc16_1_out_2));
  DEC16 dec16_1 (.in_1(OUT), .out_2(dec16_1_out_2));
  Multiplexer #(.select(2), .width(16), .disabled(0), .enable("false")) multiplexer_1 (
    .in0({16{1'b0}}), .in1({HI, LO}), .in2(inc16_1_out_2), .in3(dec16_1_out_2), .out(monitor_2),
    .sel(ctrl[31:30]));
  assign {HI_2, LO_2} = ctrl[29] ? monitor_2 : 16'bz;  // Controlled_Buffer controlled_buffer_1

  assign monitor = {HI, LO};
  assign out_6 = ctrl[28];
endmodule

module DATABUS_BUFFER (
  input  [7:0] fromExDataBus,
  input  [7:0] fromDataBus,
  input  [31:0] ctrl,
  output [7:0] monitor,
  output [7:0] toExDataBus,
  output [7:0] toDataBus
);

  wire undriven, undriven_2, undriven_3, undriven_4, undriven_5;
  wire [7:0] multiplexer_2_out, rom_1_data;

  Multiplexer #(.width(8), .disabled(0), .enable("false")) multiplexer_1 (
    .in0(fromExDataBus), .in1(fromDataBus), .out(toDataBus), .sel(undriven));
  Register register_1 (.D(toDataBus), .en(undriven_2), .Q(monitor), .clk(undriven_3));  // open: clr
  ROM #(.addrWidth(4)) rom_1 (.addr(fromDataBus[3:0]), .data(rom_1_data));  // open: sel
  Multiplexer #(.width(8), .disabled(0), .enable("false")) multiplexer_2 (
    .in1(rom_1_data), .out(multiplexer_2_out), .sel(undriven_5));  // open: in0
  assign toExDataBus = undriven_4 ? multiplexer_2_out : 8'bz;  // Controlled_Buffer controlled_buffer_1

  // Other names for the same wires on the sheet: STATE[7:0] = ctrl[23:16]

  // Notes on the sheet:
  //   STATUS WORD
  //   contents of rom_1 (hex, n*v repeats v):
  //   0 a2 82 0 86 4 2 10 23 8a 2b
endmodule

module REGISTER_SELECTOR (
  input  [31:0] ctrl,
  output [7:0] WZ_Ctrl,
  output [7:0] BC_Ctrl,
  output [7:0] DE_ctrl,
  output [7:0] HL_ctrl,
  output [7:0] SP_ctrl,
  output [7:0] PC_ctrl
);

  wire DH_Exchg_q, not_1_out, undriven, undriven_2;
  wire [3:0] multiplexer_1_out, multiplexer_2_out, undriven_3, undriven_4;

  D_Flip_Flop DH_Exchg (.clk(undriven), .D(undriven_2), .Q(DH_Exchg_q));  // open: Qn, preset, en, reset
  Multiplexer #(.width(4), .disabled(0), .enable("false")) multiplexer_1 (
    .in0(undriven_3), .in1(undriven_4), .out(multiplexer_1_out), .sel(DH_Exchg_q));
  Multiplexer #(.width(4), .disabled(0), .enable("false")) multiplexer_2 (
    .in0(undriven_4), .in1(undriven_3), .out(multiplexer_2_out), .sel(not_1_out));
  not not_1 (not_1_out, DH_Exchg_q);
endmodule

module MULTIPLEXER (
  input  [7:0] fromDATABUS,
  input  [7:0] fromREGISTER_ARRAY_hi,
  input  [7:0] fromREGISTER_ARRAY_lo,
  input  [31:0] ctrl,
  output [7:0] toREGISTER_ARRAY_hi,
  output [7:0] toREGISTER_ARRAY_lo,
  output [7:0] toDATABUS
);

  wire undriven, undriven_2, undriven_3;
  wire [7:0] multiplexer_1_out;

  assign toREGISTER_ARRAY_hi = undriven_2 ? fromDATABUS : 8'bz;  // Controlled_Buffer controlled_buffer_1
  Multiplexer #(.width(8), .disabled(0), .enable("false")) multiplexer_1 (
    .in0(fromREGISTER_ARRAY_hi), .in1(fromREGISTER_ARRAY_lo), .out(multiplexer_1_out), .sel(undriven));
  assign toDATABUS = undriven_3 ? multiplexer_1_out : 8'bz;  // Controlled_Buffer controlled_buffer_2

  assign toREGISTER_ARRAY_lo = toREGISTER_ARRAY_hi;
endmodule

module DECIMAL_ADJUST (
  input  [9:0] fromALU,
  output [9:0] toALU
);

  DAA daa_1 (.A(fromALU[9:2]), .AC(fromALU[0]), .Cin(fromALU[1]), .AC_2(toALU[0]), .Y(toALU[9:2]), .Cout(toALU[1]));
endmodule

module INSTRUCTIN_REGISTER (
  input  [7:0] OPECODEin,
  input  [31:0] ctrl,
  output [7:0] monitor,
  output [7:0] OPECODEout
);

  Register register_1 (.D(OPECODEin), .en(ctrl[6]), .Q(monitor), .clk(ctrl[8]));  // open: clr

  assign OPECODEout = monitor;
endmodule

module FLAG (
  input  [7:0] fromDATABUS,
  input  [4:0] fromALU,
  input  [23:0] ctrl,
  output [7:0] toDATABUS,
  output [7:0] toDATABUS_2,
  output [4:0] toALU,
  output [4:0] toDECODER
);

  wire undriven, undriven_2, undriven_3, undriven_4;
  wire [4:0] multiplexer_1_out;

  Multiplexer #(.width(5), .disabled(0), .enable("false")) multiplexer_1 (
    .in0({fromDATABUS[7:6], fromDATABUS[4], fromDATABUS[2], fromDATABUS[0]}), .in1(fromALU),
    .out(multiplexer_1_out), .sel(undriven_2));
  Register #(.width(1)) register_1 (.D(multiplexer_1_out[0]), .en(undriven_3), .Q(toALU[0]));  // open: clk, clr
  Register #(.width(4)) register_2 (
    .D(multiplexer_1_out[4:1]), .en(undriven), .Q(toALU[4:1]), .clk(undriven_4));  // open: clr

  assign toDATABUS = {toALU[4:3], 1'b0, toALU[2], 1'b0, toALU[1], 1'b1, toALU[0]};
  assign toDATABUS_2 = {toALU[4:3], 1'b0, toALU[2], 1'b0, toALU[1], 1'b1, toALU[0]};
  assign toDECODER = toALU;
endmodule

module ADDRESS_BUFFER (
  input  [15:0] in_1,
  input  ctrl,
  output [15:0] out_3
);

  assign out_3 = ctrl ? in_1 : 16'bz;  // Controlled_Buffer controlled_buffer_1
endmodule

module StateCtrl (
  input  [4:0] state,
  input  [2:0] stateMode,
  input  in_3,
  output [4:0] next
);

  GetNextState getnextstate_1 (.state(state), .\type (stateMode), .next(next), .SkipN1T5(in_3));
endmodule

module STATE_IND (
  input  [9:0] State_in,
  output out_2,
  output out_3,
  output out_4,
  output out_5,
  output out_6,
  output out_7,
  output out_8,
  output out_9,
  output out_10
);


  assign out_2 = State_in[0];
  assign out_3 = State_in[1];
  assign out_4 = State_in[2];
  assign out_5 = State_in[3];
  assign out_6 = State_in[4];
  assign out_7 = State_in[5];
  assign out_8 = State_in[6];
  assign out_9 = State_in[7];
  assign out_10 = State_in[8];
endmodule

module GetNextState (
  input  [4:0] state,
  input  [2:0] \type ,
  input  SkipN1T5,
  output [4:0] next
);

  wire and_1_out, and_2_out, multiplexer_3_out;
  wire [4:0] adder_1_out, multiplexer_1_out;
  wire [16:0] rom_1_data;

  // Probe on state
  Adder #(.width(5)) adder_1 (.a(state), .b({5{1'b0}}), .out(adder_1_out), .cin(1'b1));  // open: cout
  ROM #(.addrWidth(3), .dataWidth(17)) rom_1 (.addr(\type ), .data(rom_1_data));  // open: sel
  and and_1 (and_1_out, SkipN1T5, and_2_out);
  and and_2 (and_2_out, state[0], state[1], ~state[2], ~state[3], ~state[4]);  // AND_Gate
  Multiplexer #(.width(5), .disabled(0), .enable("false")) multiplexer_1 (
    .in0(adder_1_out), .in1({5{1'b0}}), .out(multiplexer_1_out), .sel(multiplexer_3_out));
  // Probe on next
  Multiplexer #(.width(5), .disabled(0), .enable("false")) multiplexer_2 (
    .in0(multiplexer_1_out), .in1(5'b00101), .out(next), .sel(and_1_out));
  // Probe on multiplexer_3_out
  Multiplexer #(.select(5), .disabled(0), .enable("false")) multiplexer_3 (
    .in0(rom_1_data[0]), .in1(rom_1_data[1]), .in2(rom_1_data[2]), .in3(rom_1_data[3]), .in4(rom_1_data[4]),
    .in5(rom_1_data[5]), .in6(rom_1_data[6]), .in7(rom_1_data[7]), .in8(rom_1_data[8]), .in9(rom_1_data[9]),
    .in10(rom_1_data[10]), .in11(rom_1_data[11]), .in12(rom_1_data[12]), .in13(rom_1_data[13]),
    .in14(rom_1_data[14]), .in15(rom_1_data[15]), .in16(rom_1_data[16]), .out(multiplexer_3_out), .sel(state));  // open: in17, in18, in19, in20, in21, in22, in23, in24, in25, in26, in27, in28, in29, in30, in31

  // Notes on the sheet:
  //   contents of rom_1 (hex, n*v repeats v):
  //   0 8 40 80 200 400 2000 10000
endmodule

module DEC4 (
  input  A3,
  input  A2,
  input  A1,
  input  A0,
  output Y,
  output Y3,
  output Y2,
  output Y1,
  output Y0
);

  wire and_1_out, and_2_out, and_3_out, and_4_out, and_5_out, and_6_out, nor_2_out, nor_3_out;

  not not_1 (Y0, A0);
  nor nor_1 (Y, A3, A2, A1, A0);
  and and_1 (and_1_out, A3, A0);
  and and_2 (and_2_out, A3, A1);
  and and_3 (and_3_out, A3, A2);
  nor nor_2 (nor_2_out, A2, A1, A0);
  and and_4 (and_4_out, A2, A0);
  and and_5 (and_5_out, A2, A1);
  nor nor_3 (nor_3_out, A1, A0);
  and and_6 (and_6_out, A1, A0);
  or or_1 (Y3, Y, and_1_out, and_2_out, and_3_out);
  or or_2 (Y2, nor_2_out, and_4_out, and_5_out);
  or or_3 (Y1, nor_3_out, and_6_out);
endmodule

// --
module DEC16 (
  input  [15:0] in_1,
  output [15:0] out_2
);

  wire and_1_out, and_2_out, dec4_1_y, dec4_2_y, dec4_3_y;
  wire [3:0] dec4_2_y0, dec4_3_y0, dec4_4_y0;

  DEC4 dec4_1 (
    .A3(in_1[3]), .A2(in_1[2]), .A1(in_1[1]), .A0(in_1[0]), .Y(dec4_1_y), .Y3(out_2[3]), .Y2(out_2[2]),
    .Y1(out_2[1]), .Y0(out_2[0]));
  DEC4 dec4_2 (
    .A3(in_1[7]), .A2(in_1[6]), .A1(in_1[5]), .A0(in_1[4]), .Y(dec4_2_y), .Y3(dec4_2_y0[3]),
    .Y2(dec4_2_y0[2]), .Y1(dec4_2_y0[1]), .Y0(dec4_2_y0[0]));
  DEC4 dec4_3 (
    .A3(in_1[11]), .A2(in_1[10]), .A1(in_1[9]), .A0(in_1[8]), .Y(dec4_3_y), .Y3(dec4_3_y0[3]),
    .Y2(dec4_3_y0[2]), .Y1(dec4_3_y0[1]), .Y0(dec4_3_y0[0]));
  DEC4 dec4_4 (
    .A3(in_1[15]), .A2(in_1[14]), .A1(in_1[13]), .A0(in_1[12]), .Y3(dec4_4_y0[3]), .Y2(dec4_4_y0[2]),
    .Y1(dec4_4_y0[1]), .Y0(dec4_4_y0[0]));  // open: Y
  and and_1 (and_1_out, dec4_1_y, dec4_2_y);
  and and_2 (and_2_out, dec4_1_y, dec4_2_y, dec4_3_y);
  Multiplexer #(.width(4), .disabled(0), .enable("false")) multiplexer_1 (
    .in0(in_1[7:4]), .in1(dec4_2_y0), .out(out_2[7:4]), .sel(dec4_1_y));
  Multiplexer #(.width(4), .disabled(0), .enable("false")) multiplexer_2 (
    .in0(in_1[11:8]), .in1(dec4_3_y0), .out(out_2[11:8]), .sel(and_1_out));
  Multiplexer #(.width(4), .disabled(0), .enable("false")) multiplexer_3 (
    .in0(in_1[15:12]), .in1(dec4_4_y0), .out(out_2[15:12]), .sel(and_2_out));
endmodule

module INC4 (
  input  A3,
  input  A2,
  input  A1,
  input  A0,
  output Y,
  output Y3,
  output Y2,
  output Y1,
  output Y0
);

  wire and_2_out, and_3_out, and_4_out, and_5_out, nand_1_out, nand_2_out;

  and and_1 (Y, A3, A2, A1, A0);
  not not_1 (Y0, A0);
  and and_2 (and_2_out, ~A3, A2, A1, A0);  // AND_Gate
  nand nand_1 (nand_1_out, A2, A1, A0);
  and and_3 (and_3_out, ~A2, A1, A0);  // AND_Gate
  and and_4 (and_4_out, A2, nand_2_out);
  nand nand_2 (nand_2_out, A0, A1);
  or or_1 (Y3, and_2_out, and_5_out);
  and and_5 (and_5_out, A3, nand_1_out);
  or or_2 (Y2, and_3_out, and_4_out);
  xor xor_1 (Y1, A0, A1);
endmodule

// ++
module INC16 (
  input  [15:0] in_1,
  output [15:0] out_2
);

  wire and_1_out, and_2_out, inc4_1_y, inc4_2_y, inc4_3_y;
  wire [3:0] inc4_2_y0, inc4_3_y0, inc4_4_y0;

  INC4 inc4_1 (
    .A3(in_1[3]), .A2(in_1[2]), .A1(in_1[1]), .A0(in_1[0]), .Y(inc4_1_y), .Y3(out_2[3]), .Y2(out_2[2]),
    .Y1(out_2[1]), .Y0(out_2[0]));
  INC4 inc4_2 (
    .A3(in_1[7]), .A2(in_1[6]), .A1(in_1[5]), .A0(in_1[4]), .Y(inc4_2_y), .Y3(inc4_2_y0[3]),
    .Y2(inc4_2_y0[2]), .Y1(inc4_2_y0[1]), .Y0(inc4_2_y0[0]));
  INC4 inc4_3 (
    .A3(in_1[11]), .A2(in_1[10]), .A1(in_1[9]), .A0(in_1[8]), .Y(inc4_3_y), .Y3(inc4_3_y0[3]),
    .Y2(inc4_3_y0[2]), .Y1(inc4_3_y0[1]), .Y0(inc4_3_y0[0]));
  INC4 inc4_4 (
    .A3(in_1[15]), .A2(in_1[14]), .A1(in_1[13]), .A0(in_1[12]), .Y3(inc4_4_y0[3]), .Y2(inc4_4_y0[2]),
    .Y1(inc4_4_y0[1]), .Y0(inc4_4_y0[0]));  // open: Y
  and and_1 (and_1_out, inc4_1_y, inc4_2_y);
  and and_2 (and_2_out, inc4_1_y, inc4_2_y, inc4_3_y);
  Multiplexer #(.width(4), .disabled(0), .enable("false")) multiplexer_1 (
    .in0(in_1[7:4]), .in1(inc4_2_y0), .out(out_2[7:4]), .sel(inc4_1_y));
  Multiplexer #(.width(4), .disabled(0), .enable("false")) multiplexer_2 (
    .in0(in_1[11:8]), .in1(inc4_3_y0), .out(out_2[11:8]), .sel(and_1_out));
  Multiplexer #(.width(4), .disabled(0), .enable("false")) multiplexer_3 (
    .in0(in_1[15:12]), .in1(inc4_4_y0), .out(out_2[15:12]), .sel(and_2_out));
endmodule

module StateDecoder (
  input  [4:0] A,
  output [2:0] M,
  output [1:0] T
);

  wire and_1_out, and_2_out, and_3_out, and_4_out, and_5_out, and_6_out, and_7_out, and_8_out, and_9_out,
       and_10_out, and_11_out, and_12_out, and_13_out, and_14_out, and_15_out, and_16_out, and_17_out,
       and_18_out, and_19_out, and_20_out, and_21_out, and_22_out, and_23_out, and_24_out, and_25_out,
       not_1_out, not_2_out, not_3_out, not_4_out, not_5_out, not_6_out, not_7_out, not_8_out, not_9_out,
       not_10_out, not_11_out, not_12_out, not_13_out, not_14_out, not_15_out, not_16_out, not_17_out,
       not_18_out, not_19_out, not_20_out, not_21_out, not_22_out, not_23_out, not_24_out, not_25_out,
       not_26_out, not_27_out, not_28_out, not_29_out, not_30_out, not_31_out, not_32_out, not_33_out,
       not_34_out, not_35_out, not_36_out, not_37_out, not_38_out, not_39_out, not_40_out, not_41_out,
       not_42_out, not_43_out, not_44_out, not_45_out, not_46_out, not_47_out, not_48_out, not_49_out,
       not_50_out, not_51_out, not_52_out, not_53_out, not_54_out, not_55_out, not_56_out, not_57_out,
       not_58_out, not_59_out, not_60_out, not_61_out, not_62_out, not_63_out, not_64_out, not_65_out,
       not_66_out;

  not not_1 (not_1_out, A[4]);
  not not_2 (not_2_out, A[3]);
  not not_3 (not_3_out, A[2]);
  not not_4 (not_4_out, A[1]);
  not not_5 (not_5_out, A[3]);
  not not_6 (not_6_out, A[2]);
  not not_7 (not_7_out, A[0]);
  not not_8 (not_8_out, A[4]);
  not not_9 (not_9_out, A[3]);
  not not_10 (not_10_out, A[4]);
  not not_11 (not_11_out, A[3]);
  not not_12 (not_12_out, A[4]);
  not not_13 (not_13_out, A[2]);
  not not_14 (not_14_out, A[1]);
  not not_15 (not_15_out, A[4]);
  not not_16 (not_16_out, A[2]);
  not not_17 (not_17_out, A[0]);
  not not_18 (not_18_out, A[3]);
  not not_19 (not_19_out, A[2]);
  not not_20 (not_20_out, A[1]);
  not not_21 (not_21_out, A[3]);
  not not_22 (not_22_out, A[2]);
  not not_23 (not_23_out, A[0]);
  not not_24 (not_24_out, A[4]);
  not not_25 (not_25_out, A[3]);
  not not_26 (not_26_out, A[2]);
  not not_27 (not_27_out, A[4]);
  not not_28 (not_28_out, A[3]);
  not not_29 (not_29_out, A[1]);
  not not_30 (not_30_out, A[0]);
  not not_31 (not_31_out, A[4]);
  not not_32 (not_32_out, A[2]);
  not not_33 (not_33_out, A[1]);
  not not_34 (not_34_out, A[4]);
  not not_35 (not_35_out, A[2]);
  not not_36 (not_36_out, A[0]);
  not not_37 (not_37_out, A[4]);
  not not_38 (not_38_out, A[3]);
  not not_39 (not_39_out, A[2]);
  not not_40 (not_40_out, A[1]);
  not not_41 (not_41_out, A[0]);
  not not_42 (not_42_out, A[4]);
  not not_43 (not_43_out, A[2]);
  not not_44 (not_44_out, A[0]);
  not not_45 (not_45_out, A[4]);
  not not_46 (not_46_out, A[3]);
  not not_47 (not_47_out, A[4]);
  not not_48 (not_48_out, A[1]);
  not not_49 (not_49_out, A[3]);
  not not_50 (not_50_out, A[2]);
  not not_51 (not_51_out, A[1]);
  not not_52 (not_52_out, A[0]);
  not not_53 (not_53_out, A[4]);
  not not_54 (not_54_out, A[2]);
  not not_55 (not_55_out, A[1]);
  not not_56 (not_56_out, A[4]);
  not not_57 (not_57_out, A[3]);
  not not_58 (not_58_out, A[0]);
  not not_59 (not_59_out, A[4]);
  not not_60 (not_60_out, A[1]);
  not not_61 (not_61_out, A[0]);
  not not_62 (not_62_out, A[4]);
  not not_63 (not_63_out, A[3]);
  not not_64 (not_64_out, A[2]);
  not not_65 (not_65_out, A[0]);
  and and_1 (and_1_out, not_1_out, A[3], A[1], A[0]);
  not not_66 (not_66_out, A[4]);
  and and_2 (and_2_out, not_66_out, A[3], A[2]);
  and and_3 (and_3_out, A[4], not_2_out, not_3_out, not_4_out);
  and and_4 (and_4_out, A[4], not_5_out, not_6_out, not_7_out);
  and and_5 (and_5_out, not_8_out, not_9_out, A[2], A[0]);
  and and_6 (and_6_out, not_10_out, not_11_out, A[2], A[1]);
  and and_7 (and_7_out, not_12_out, A[3], not_13_out, not_14_out);
  and and_8 (and_8_out, not_15_out, A[3], not_16_out, not_17_out);
  and and_9 (and_9_out, A[4], not_18_out, not_19_out, not_20_out, A[0]);
  and and_10 (and_10_out, A[4], not_21_out, not_22_out, A[1], not_23_out);
  and and_11 (and_11_out, not_24_out, not_25_out, not_26_out, A[1], A[0]);
  and and_12 (and_12_out, not_27_out, not_28_out, A[2], not_29_out, not_30_out);
  and and_13 (and_13_out, not_31_out, A[3], not_32_out, not_33_out);
  and and_14 (and_14_out, not_34_out, A[3], not_35_out, not_36_out);
  and and_15 (and_15_out, not_37_out, A[3], A[2], A[1]);
  and and_16 (and_16_out, A[4], not_38_out, not_39_out, not_40_out, not_41_out);
  and and_17 (and_17_out, not_42_out, not_43_out, A[1], not_44_out);
  and and_18 (and_18_out, not_45_out, not_46_out, A[2], A[1], A[0]);
  and and_19 (and_19_out, not_47_out, A[3], A[2], not_48_out, A[0]);
  and and_20 (and_20_out, A[4], not_49_out, not_50_out, not_51_out, not_52_out);
  and and_21 (and_21_out, not_53_out, not_54_out, not_55_out, A[0]);
  and and_22 (and_22_out, not_56_out, not_57_out, A[2], not_58_out);
  and and_23 (and_23_out, not_59_out, A[2], not_60_out, not_61_out);
  and and_24 (and_24_out, not_62_out, A[3], A[2], A[1], A[0]);
  and and_25 (and_25_out, A[4], not_63_out, not_64_out, A[1], not_65_out);
  or or_1 (M[2], and_1_out, and_2_out, and_3_out, and_4_out);
  or or_2 (T[1], and_17_out, and_18_out, and_19_out, and_20_out);
  or or_3 (T[0], and_21_out, and_22_out, and_23_out, and_24_out, and_25_out);
  or or_4 (M[1], and_5_out, and_6_out, and_7_out, and_8_out, and_9_out, and_10_out);
  or or_5 (M[0], and_11_out, and_12_out, and_13_out, and_14_out, and_15_out, and_16_out);
endmodule
